# Fritzing sketch innlevering 2 (saved by Fritzing 0.9.3b)
breadboards: 1

parts:
  Part1 = Arduino Uno (Rev3) - ICSP
  ZS-042_RTC1 = ZS-042 RTC Module
  J1 = Piezo Speaker  # not connected

nets:
  N1: Part1.A4/SDA, ZS-042_RTC1.SDA
  N2: Part1.A5/SCL, ZS-042_RTC1.SCL
  GND: Part1.GND, ZS-042_RTC1.GND
  5V: Part1.5V, ZS-042_RTC1.VCC

notes:
  Fant dessverre ikke TFT skjermen ST7735, men tegna koblingene sånn som jeg gjorde det. Skjermen skal begynne helt fra nedre høyre side, helt frem til den siste rød VCCen
